# Fritzing sketch Enkoder (saved by Fritzing 0.9.8b)
breadboards: 1

parts:
  J1 = JST-03JQ-BT [part_number=JST-JQ-BT package=THT]
  C1 = Electrolytic Capacitor [capacitance=10µF voltage=50V package="0405 [SMD, electrolytic]"]
  R1 = Resistor [tolerance=±5% resistance=220 package="1206 [SMD]"]
  R2 = Resistor [tolerance=±5% resistance=3.3k package="1206 [SMD]"]
  Part1 = Arduino Nano (Rev3.0)
  C2 = Capacitor [part_number=22n package=cap-pth-small2]
  LM1 = LM393 [chip_label=?]
  R4 = Resistor [tolerance=±5% resistance=10k package="1206 [SMD]"]
  R5 = Resistor [tolerance=±5% resistance=10k package="1206 [SMD]"]

nets:
  N1: J1.pin2, C1.-, Part1.GND
  N2: J1.pin1, R1.Pin_1
  N3: J1.pin3, C1.+, R2.Pin_1
  3V3: R1.Pin_0, R2.Pin_0, Part1.3V3, LM1.VCC, R4.Pin_1
  N4: Part1.D2, C2.2, LM1.Output_1
  N5: C2.1, LM1.GND
  N6: LM1.In_1_-, R4.Pin_0, R5.Pin_1

notes:
  zielony - dzielnik napięcia i A-
  żółty A+
  pomarańczowy -wyjście
